// Logisim project 7seg.circ as structural Verilog: 11 circuits, main circuit b2d
module main (
  input  in_1,
  output [6:0] digit_1,
  output [6:0] digit2,
  output [6:0] digit3,
  output [6:0] digit_4
);

  wire CLK_sig_out;
  wire [2:0] seven2two_1_out_3, seven2two_2_out_3, seven2two_3_out_3, seven2two_4_out_3;
  wire [3:0] seven2two_1_out_2, seven2two_2_out_2, seven2two_3_out_2, seven2two_4_out_2;
  wire [6:0] out_structure_1_out_6;

  Clock CLK_sig (.out(CLK_sig_out));
  out_structure out_structure_1 (
    .in_1(in_1), .in_2(CLK_sig_out), .out_3(digit_1), .out_4(digit2), .out_5(digit3),
    .out_6(out_structure_1_out_6));
  seven2two seven2two_1 (.in_1(out_structure_1_out_6), .out_2(seven2two_1_out_2), .out_3(seven2two_1_out_3));
  seven2two seven2two_2 (.in_1(digit3), .out_2(seven2two_2_out_2), .out_3(seven2two_2_out_3));
  seven2two seven2two_3 (.in_1(digit2), .out_2(seven2two_3_out_2), .out_3(seven2two_3_out_3));
  seven2two seven2two_4 (.in_1(digit_1), .out_2(seven2two_4_out_2), .out_3(seven2two_4_out_3));
  _7_Segment_Display u_7_segment_display_1 (
    .g(seven2two_1_out_2[0]), .f(seven2two_1_out_2[1]), .a(seven2two_1_out_2[2]), .b(seven2two_1_out_2[3]),
    .e(seven2two_1_out_3[0]), .d(seven2two_1_out_3[1]), .c(seven2two_1_out_3[2]));  // open: dp
  _7_Segment_Display u_7_segment_display_2 (
    .g(seven2two_2_out_2[0]), .f(seven2two_2_out_2[1]), .a(seven2two_2_out_2[2]), .b(seven2two_2_out_2[3]),
    .e(seven2two_2_out_3[0]), .d(seven2two_2_out_3[1]), .c(seven2two_2_out_3[2]));  // open: dp
  _7_Segment_Display u_7_segment_display_3 (
    .g(seven2two_3_out_2[0]), .f(seven2two_3_out_2[1]), .a(seven2two_3_out_2[2]), .b(seven2two_3_out_2[3]),
    .e(seven2two_3_out_3[0]), .d(seven2two_3_out_3[1]), .c(seven2two_3_out_3[2]));  // open: dp
  _7_Segment_Display u_7_segment_display_4 (
    .g(seven2two_4_out_2[0]), .f(seven2two_4_out_2[1]), .a(seven2two_4_out_2[2]), .b(seven2two_4_out_2[3]),
    .e(seven2two_4_out_3[0]), .d(seven2two_4_out_3[1]), .c(seven2two_4_out_3[2]));  // open: dp

  assign digit_4 = digit_1;
endmodule

module b2d (
  input  in_1,
  input  C,
  input  in_3,
  input  in_4,
  output a,
  output b,
  output out_7,
  output d,
  output e,
  output f,
  output g
);

  wire and_1_out, and_2_out, and_3_out, and_4_out, and_5_out, and_6_out, and_7_out, and_8_out, and_9_out,
       and_10_out, and_11_out, and_12_out, and_13_out, and_14_out, and_15_out, and_16_out, and_17_out,
       and_18_out, and_19_out, and_20_out, and_21_out, and_22_out, and_23_out, and_24_out, and_25_out,
       and_26_out, not_1_out, not_2_out, not_3_out, not_4_out;

  not not_1 (not_1_out, in_1);
  not not_2 (not_2_out, C);
  not not_3 (not_3_out, in_3);
  not not_4 (not_4_out, in_4);
  and and_1 (and_1_out, not_1_out, in_3);
  and and_2 (and_2_out, not_1_out, C, in_4);
  and and_3 (and_3_out, in_1, not_2_out, not_3_out);
  and and_4 (and_4_out, not_1_out, not_2_out, not_4_out);
  and and_5 (and_5_out, not_1_out, not_2_out);
  and and_6 (and_6_out, not_1_out, not_3_out, not_4_out);
  and and_7 (and_7_out, not_1_out, in_3, in_4);
  and and_8 (and_8_out, not_2_out, not_3_out);
  and and_9 (and_9_out, not_1_out, in_4);
  and and_10 (and_10_out, not_1_out, C);
  and and_11 (and_11_out, not_2_out, not_3_out);
  and and_12 (and_12_out, not_1_out, not_2_out, in_3);
  and and_13 (and_13_out, not_1_out, C, not_3_out, in_4);
  and and_14 (and_14_out, not_1_out, in_3, not_4_out);
  and and_15 (and_15_out, in_1, not_2_out, not_3_out);
  and and_16 (and_16_out, not_1_out, not_2_out, not_4_out);
  and and_17 (and_17_out, not_1_out, in_3, not_4_out);
  and and_18 (and_18_out, not_2_out, not_3_out, not_4_out);
  and and_19 (and_19_out, not_1_out, C, not_3_out);
  and and_20 (and_20_out, not_1_out, C, not_4_out);
  and and_21 (and_21_out, in_1, not_2_out, not_3_out);
  and and_22 (and_22_out, not_1_out, not_3_out, not_4_out);
  and and_23 (and_23_out, not_1_out, not_2_out, in_3);
  and and_24 (and_24_out, not_1_out, C, not_3_out);
  and and_25 (and_25_out, in_1, not_2_out, not_3_out);
  and and_26 (and_26_out, not_1_out, in_3, not_4_out);
  or or_1 (a, and_1_out, and_2_out, and_3_out, and_4_out);
  or or_2 (b, and_5_out, and_6_out, and_7_out, and_8_out);
  or or_3 (out_7, and_9_out, and_10_out, and_11_out);
  or or_4 (d, and_12_out, and_13_out, and_14_out, and_15_out, and_16_out);
  or or_5 (e, and_17_out, and_18_out);
  or or_6 (f, and_19_out, and_20_out, and_21_out, and_22_out);
  or or_7 (g, and_23_out, and_24_out, and_25_out, and_26_out);
endmodule

module binary_tranform (
  input  b,
  input  C,
  input  in_3,
  input  in_4,
  output g,
  output f,
  output a,
  output x,
  output e,
  output d,
  output y
);

  wire and_1_out, and_2_out, and_3_out, and_4_out, and_5_out, and_6_out, and_7_out, and_8_out, and_9_out,
       and_10_out, and_11_out, and_12_out, and_13_out, and_14_out, and_15_out, and_16_out, and_17_out,
       and_18_out, and_19_out, and_20_out, and_21_out, and_22_out, and_23_out, and_24_out, and_25_out,
       and_26_out, not_1_out, not_2_out, not_3_out, not_4_out;

  not not_1 (not_1_out, b);
  not not_2 (not_2_out, C);
  not not_3 (not_3_out, in_3);
  not not_4 (not_4_out, in_4);
  and and_1 (and_1_out, not_1_out, not_2_out, in_3);
  and and_2 (and_2_out, not_1_out, C, not_3_out);
  and and_3 (and_3_out, b, not_2_out, not_3_out);
  and and_4 (and_4_out, not_1_out, in_3, not_4_out);
  and and_5 (and_5_out, not_1_out, C, not_3_out);
  and and_6 (and_6_out, not_1_out, C, not_4_out);
  and and_7 (and_7_out, b, not_2_out, not_3_out);
  and and_8 (and_8_out, not_1_out, not_3_out, not_4_out);
  and and_9 (and_9_out, not_1_out, in_3);
  and and_10 (and_10_out, not_1_out, C, in_4);
  and and_11 (and_11_out, b, not_2_out, not_3_out);
  and and_12 (and_12_out, not_1_out, not_2_out, not_4_out);
  and and_13 (and_13_out, not_1_out, not_2_out);
  and and_14 (and_14_out, not_1_out, not_3_out, not_4_out);
  and and_15 (and_15_out, not_1_out, in_3, in_4);
  and and_16 (and_16_out, not_2_out, not_3_out);
  and and_17 (and_17_out, not_1_out, in_3, not_4_out);
  and and_18 (and_18_out, not_2_out, not_3_out, not_4_out);
  and and_19 (and_19_out, not_1_out, not_2_out, in_3);
  and and_20 (and_20_out, not_1_out, C, not_3_out, in_4);
  and and_21 (and_21_out, not_1_out, in_3, not_4_out);
  and and_22 (and_22_out, b, not_2_out, not_3_out);
  and and_23 (and_23_out, not_1_out, not_2_out, not_4_out);
  and and_24 (and_24_out, not_1_out, in_4);
  and and_25 (and_25_out, not_1_out, C);
  and and_26 (and_26_out, not_2_out, not_3_out);
  or or_1 (g, and_1_out, and_2_out, and_3_out, and_4_out);
  or or_2 (f, and_5_out, and_6_out, and_7_out, and_8_out);
  or or_3 (a, and_9_out, and_10_out, and_11_out, and_12_out);
  or or_4 (x, and_13_out, and_14_out, and_15_out, and_16_out);
  or or_5 (e, and_17_out, and_18_out);
  or or_6 (d, and_19_out, and_20_out, and_21_out, and_22_out, and_23_out);
  or or_7 (y, and_24_out, and_25_out, and_26_out);
endmodule

module out_structure (
  input  in_1,
  input  in_2,
  output [6:0] out_3,
  output [6:0] out_4,
  output [6:0] out_5,
  output [6:0] out_6
);

  wire and_1_out, not_1_out, not_2_out, replicate_for_out_structure_1_out_3,
       replicate_for_out_structure_3_out_3;
  wire [3:0] decade_count_logic_1_out_3, register_1_q;

  Register #(.width(4)) register_1 (
    .D(decade_count_logic_1_out_3), .en(1'b1), .clk(in_2), .Q(register_1_q));  // open: clr
  replicate_for_out_structure replicate_for_out_structure_1 (
    .in_1(replicate_for_out_structure_3_out_3), .out_2(out_5), .out_3(replicate_for_out_structure_1_out_3));
  not not_1 (not_1_out, register_1_q[2]);
  replicate_for_out_structure replicate_for_out_structure_2 (
    .in_1(replicate_for_out_structure_1_out_3), .out_2(out_6));  // open: out_3
  // Probe on decade_count_logic_1_out_3
  decade_count_logic decade_count_logic_1 (.in_1(in_2), .res(in_1), .out_3(decade_count_logic_1_out_3));
  not not_2 (not_2_out, register_1_q[1]);
  // Probe on register_1_q
  and and_1 (and_1_out, register_1_q[3], not_1_out, not_2_out, register_1_q[0], in_2);
  binary_tranform binary_tranform_1 (
    .b(register_1_q[3]), .C(register_1_q[2]), .in_3(register_1_q[1]), .in_4(register_1_q[0]), .g(out_3[0]),
    .f(out_3[1]), .a(out_3[2]), .x(out_3[3]), .e(out_3[4]), .d(out_3[5]), .y(out_3[6]));
  replicate_for_out_structure replicate_for_out_structure_3 (
    .in_1(and_1_out), .out_2(out_4), .out_3(replicate_for_out_structure_3_out_3));
endmodule

module working_sequence (
  input  in_1,
  output [3:0] out_2
);

  wire [4:0] counter_1_q;

  Counter #(.max('h1f), .width(5)) counter_1 (.Q(counter_1_q), .clk(in_1));  // open: load, D, count, carry, up, clr
  ROM #(.addrWidth(5), .dataWidth(4)) rom_1 (.addr(counter_1_q), .data(out_2));

  // Notes on the sheet:
  //   contents of rom_1 (hex, n*v repeats v):
  //   0 1 2 3 4 5 6 7 8 9 0 0 1 2 3 4 5 6 7 8 9 0 0 1 2 3 4 5 6 7 8 9
endmodule

module seven2two (
  input  [6:0] in_1,
  output [3:0] out_2,
  output [2:0] out_3
);


  assign out_2 = in_1[3:0];
  assign out_3 = in_1[6:4];
endmodule

module test (
  input  in_1
);

  wire clock_1_out;
  wire [2:0] binary_tranform_1_e;
  wire [3:0] binary_tranform_1_g, decade_count_logic_1_out_3, register_1_q;

  Clock clock_1 (.out(clock_1_out));
  decade_count_logic decade_count_logic_1 (.in_1(clock_1_out), .out_3(decade_count_logic_1_out_3));  // open: res
  Register #(.width(4)) register_1 (
    .D(decade_count_logic_1_out_3), .en(in_1), .clk(clock_1_out), .Q(register_1_q));  // open: clr
  binary_tranform binary_tranform_1 (
    .b(register_1_q[3]), .C(register_1_q[2]), .in_3(register_1_q[1]), .in_4(register_1_q[0]),
    .g(binary_tranform_1_g[0]), .f(binary_tranform_1_g[1]), .a(binary_tranform_1_g[2]),
    .x(binary_tranform_1_g[3]), .e(binary_tranform_1_e[0]), .d(binary_tranform_1_e[1]),
    .y(binary_tranform_1_e[2]));
  _7_Segment_Display u_7_segment_display_1 (
    .g(binary_tranform_1_g[0]), .f(binary_tranform_1_g[1]), .a(binary_tranform_1_g[2]),
    .b(binary_tranform_1_g[3]), .e(binary_tranform_1_e[0]), .d(binary_tranform_1_e[1]),
    .c(binary_tranform_1_e[2]));  // open: dp
endmodule

module y_out_logic (
);

  wire and_1_out, not_1_out, not_2_out, undriven, undriven_2, undriven_3, undriven_4, undriven_5;

  not not_1 (not_1_out, undriven_2);
  not not_2 (not_2_out, undriven_3);
  and and_1 (and_1_out, undriven, not_1_out, not_2_out, undriven_4, undriven_5);
endmodule

module replicate_for_out_structure (
  input  in_1,
  output [6:0] out_2,
  output out_3
);

  wire not_1_out, not_2_out;
  wire [3:0] decade_count_logic_1_out_3, register_1_q;

  Register #(.width(4)) register_1 (
    .D(decade_count_logic_1_out_3), .en(in_1), .clk(in_1), .Q(register_1_q));  // open: clr
  // Probe on decade_count_logic_1_out_3
  decade_count_logic decade_count_logic_1 (.in_1(in_1), .out_3(decade_count_logic_1_out_3));  // open: res
  not not_1 (not_1_out, register_1_q[2]);
  // Probe on register_1_q
  not not_2 (not_2_out, register_1_q[1]);
  binary_tranform binary_tranform_1 (
    .b(register_1_q[3]), .C(register_1_q[2]), .in_3(register_1_q[1]), .in_4(register_1_q[0]), .g(out_2[0]),
    .f(out_2[1]), .a(out_2[2]), .x(out_2[3]), .e(out_2[4]), .d(out_2[5]), .y(out_2[6]));
  and and_1 (out_3, register_1_q[3], not_1_out, not_2_out, register_1_q[0], in_1);
endmodule

module replicate_end (
  input  in_1,
  output [6:0] out_2
);

  wire [3:0] register_1_q, working_sequence_1_out_2;

  Register #(.width(4)) register_1 (
    .D(working_sequence_1_out_2), .en(in_1), .clk(in_1), .Q(register_1_q));  // open: clr
  // Probe on working_sequence_1_out_2
  working_sequence working_sequence_1 (.in_1(in_1), .out_2(working_sequence_1_out_2));
  // Probe on register_1_q
  binary_tranform binary_tranform_1 (
    .b(register_1_q[3]), .C(register_1_q[2]), .in_3(register_1_q[1]), .in_4(register_1_q[0]), .g(out_2[0]),
    .f(out_2[1]), .a(out_2[2]), .x(out_2[3]), .e(out_2[4]), .d(out_2[5]), .y(out_2[6]));
endmodule

module decade_count_logic (
  input  in_1,
  input  res,
  output [3:0] out_3
);

  wire and_1_out, d_ff_1_qn, d_ff_2_qn, d_ff_3_qn, d_ff_4_qn, or_1_out;

  D_Flip_Flop d_ff_1 (.D(d_ff_1_qn), .clk(in_1), .Q(out_3[0]), .Qn(d_ff_1_qn), .reset(or_1_out));  // open: preset
  or or_1 (or_1_out, res, and_1_out);
  D_Flip_Flop d_ff_2 (.D(d_ff_2_qn), .clk(d_ff_1_qn), .Q(out_3[1]), .Qn(d_ff_2_qn), .reset(or_1_out));  // open: preset
  D_Flip_Flop d_ff_3 (.D(d_ff_3_qn), .clk(d_ff_2_qn), .Q(out_3[2]), .Qn(d_ff_3_qn), .reset(or_1_out));  // open: preset
  D_Flip_Flop d_ff_4 (.D(d_ff_4_qn), .clk(d_ff_3_qn), .Q(out_3[3]), .Qn(d_ff_4_qn), .reset(or_1_out));  // open: preset
  and and_1 (and_1_out, out_3[3], out_3[1]);
endmodule
